// Logisim project 150120008_150120066_150120070.circ as structural Verilog: 23 circuits, main circuit main
module main (
);

  wire alu_1_add, alu_1_and, alu_1_is_alu_led, alu_1_is_imm_led, alu_1_nand, alu_1_nor, CLCK, cmp_1_cf,
       cmp_1_is_cmp_2, cmp_1_zf, cmp_1_zf_led, cu_1_clock_cmp, cu_1_clock_memory, cu_1_clock_pc,
       cu_1_clock_regfile, cu_1_is_alu, cu_1_is_cmp, cu_1_is_imm, cu_1_is_jump, cu_1_is_ld,
       cu_1_is_reset_cmp, cu_1_is_reset_led, cu_1_is_reset_regfile, cu_1_is_st, cu_1_is_write_regfile,
       cu_1_memory_enable, cu_1_next_ins, cu_1_next_ins_led, cu_1_pc_enable, cu_1_reset_pc, memory_1_is_ld_2,
       memory_1_is_st_2, memory_1_memory_enable_2, pc_1_is_jump_2, pc_1_pc_enable_2,
       register_file_1_write_enable_2, RESET;
  wire [1:0] cu_1_alu_opr_type;
  wire [3:0] cu_1_dst_src, cu_1_read_reg1, cu_1_read_reg2, register_file_1_destination;
  wire [9:0] cu_1_address, cu_1_ram_address, instruction_memory_1_address_2, memory_1_address_2,
       pc_1_current_address, pc_1_current_address_2;
  wire [17:0] alu_1_alu_r1, alu_1_alu_r2, alu_1_result, alu_1_result_2, cmp_1_op1_2, cmp_1_op2_2,
       cu_1_alu_r1, cu_1_alu_r2, cu_1_data_to_reg_file, cu_1_op1, cu_1_op2, cu_1_ram_data,
       instruction_memory_1_data, memory_1_data_in_2, memory_1_data_out, memory_1_data_out_2,
       register_file_1_data_2, register_file_1_read_reg_1_value, register_file_1_read_reg_1_value_2,
       register_file_1_read_reg_2_value, register_file_1_read_reg_2_value_2;

  Clock CLOCK (.out(CLCK));
  Button u_RESET (.out(RESET));
  LED WRITE_ENABLE (.in(register_file_1_write_enable_2));
  // Probe on register_file_1_read_reg_1_value_2
  // Probe on register_file_1_read_reg_2_value_2
  // Probe on register_file_1_data_2
  // Probe on register_file_1_destination
  REGISTER_FILE register_file_1 (
    .CLCK(cu_1_clock_regfile), .DATA(cu_1_data_to_reg_file),
    .READ_REG_1_VALUE(register_file_1_read_reg_1_value), .REG_1(cu_1_read_reg1),
    .WRITE_ENABLE(cu_1_is_write_regfile), .RESET_ENABLE(cu_1_is_reset_regfile), .REG_2(cu_1_read_reg2),
    .READ_REG_2_VALUE(register_file_1_read_reg_2_value), .SELECT_REGISTER(cu_1_dst_src),
    .READ_REG_1_VALUE_2(register_file_1_read_reg_1_value_2),
    .READ_REG_2_VALUE_2(register_file_1_read_reg_2_value_2), .DATA_2(register_file_1_data_2),
    .DESTINATION(register_file_1_destination), .WRITE_ENABLE_2(register_file_1_write_enable_2));
  LED IS_ALU (.in(alu_1_is_alu_led));
  // Probe on alu_1_alu_r1
  // Probe on alu_1_alu_r2
  // Probe on alu_1_result_2
  // Probe on pc_1_current_address_2
  LED IS_JUMP (.in(pc_1_is_jump_2));
  LED IS_IMM (.in(alu_1_is_imm_led));
  PC pc_1 (
    .ADDRESS(cu_1_address), .PC_ENABLE(cu_1_pc_enable), .CLCK(cu_1_clock_pc),
    .CURRENT_ADDRESS_2(pc_1_current_address_2), .RESET(cu_1_reset_pc), .IS_JUMP(cu_1_is_jump),
    .PC_ENABLE_2(pc_1_pc_enable_2), .CURRENT_ADDRESS(pc_1_current_address), .NEXT(cu_1_next_ins),
    .IS_JUMP_2(pc_1_is_jump_2));
  LED PC_ENABLE (.in(pc_1_pc_enable_2));
  ALU alu_1 (
    .R1(cu_1_alu_r1), .R2(cu_1_alu_r2), .ALU_OPR_TYPE(cu_1_alu_opr_type), .RESULT(alu_1_result),
    .IS_ALU(cu_1_is_alu), .IS_ALU_LED(alu_1_is_alu_led), .ALU_R1(alu_1_alu_r1), .ALU_R2(alu_1_alu_r2),
    .RESULT_2(alu_1_result_2), .NOR(alu_1_nor), .NAND(alu_1_nand), .AND(alu_1_and), .ADD(alu_1_add),
    .IS_IMM(cu_1_is_imm), .IS_IMM_LED(alu_1_is_imm_led));
  LED ADD (.in(alu_1_add));
  LED AND (.in(alu_1_and));
  LED NAND (.in(alu_1_nand));
  LED NOR (.in(alu_1_nor));
  LED RESET_2 (.in(cu_1_is_reset_led));
  LED IS_CMP (.in(cmp_1_is_cmp_2));
  LED NEXT (.in(cu_1_next_ins_led));
  // Probe on cmp_1_op1_2
  CMP cmp_1 (
    .IS_CMP(cu_1_is_cmp), .OP1(cu_1_op1), .OP2(cu_1_op2), .CF(cmp_1_cf), .IS_CMP_2(cmp_1_is_cmp_2),
    .CF_LED(cmp_1_cf), .OP1_2(cmp_1_op1_2), .OP2_2(cmp_1_op2_2), .ZF(cmp_1_zf), .ZF_LED(cmp_1_zf_led),
    .CLCK(cu_1_clock_cmp), .RESET(cu_1_is_reset_cmp));
  // Probe on cmp_1_op2_2
  LED ZF (.in(cmp_1_zf_led));
  LED CF (.in(cmp_1_cf));
  CU cu_1 (
    .IR_VALUE(instruction_memory_1_data), .SRC1_VALUE(register_file_1_read_reg_1_value),
    .SRC2_VALUE(register_file_1_read_reg_2_value), .ALU_RESULT_VALUE(alu_1_result),
    .VALUE_FROM_RAM(memory_1_data_out_2), .IS_ALU(cu_1_is_alu), .IS_WRITE_REGFILE(cu_1_is_write_regfile),
    .READ_REG1(cu_1_read_reg1), .READ_REG2(cu_1_read_reg2), .ADDRESS(cu_1_address), .IS_LD(cu_1_is_ld),
    .IS_ST(cu_1_is_st), .DST_SRC(cu_1_dst_src), .NEXT_INS(cu_1_next_ins),
    .DATA_TO_REG_FILE(cu_1_data_to_reg_file), .ALU_R1(cu_1_alu_r1), .ALU_R2(cu_1_alu_r2),
    .ALU_OPR_TYPE(cu_1_alu_opr_type), .RAM_ADDRESS(cu_1_ram_address), .PC_ENABLE(cu_1_pc_enable),
    .MEMORY_ENABLE(cu_1_memory_enable), .RAM_DATA(cu_1_ram_data), .CLOCK(CLCK), .IS_JUMP(cu_1_is_jump),
    .CLOCK_REGFILE(cu_1_clock_regfile), .CLOCK_PC(cu_1_clock_pc), .IS_CMP(cu_1_is_cmp), .IS_IMM(cu_1_is_imm),
    .CLOCK_MEMORY(cu_1_clock_memory), .NEXT_INS_LED(cu_1_next_ins_led),
    .IS_RESET_REGFILE(cu_1_is_reset_regfile), .IS_RESET_LED(cu_1_is_reset_led), .RESET_MANUEL(RESET),
    .RESET_PC(cu_1_reset_pc), .OP1(cu_1_op1), .OP2(cu_1_op2), .ZF(cmp_1_zf), .CF(cmp_1_cf),
    .CLOCK_CMP(cu_1_clock_cmp), .IS_RESET_CMP(cu_1_is_reset_cmp));
  INSTRUCTION_MEMORY instruction_memory_1 (
    .ADDRESS(pc_1_current_address), .DATA(instruction_memory_1_data),
    .ADDRESS_2(instruction_memory_1_address_2));
  // Probe on instruction_memory_1_data
  // Probe on instruction_memory_1_address_2
  MEMORY memory_1 (
    .ADDRESS_2(memory_1_address_2), .ADDRESS(cu_1_ram_address), .DATA_IN(cu_1_ram_data),
    .MEMORY_ENABLE(cu_1_memory_enable), .IS_ST(cu_1_is_st), .CLCK(cu_1_clock_memory), .IS_LD(cu_1_is_ld),
    .DATA_OUT_2(memory_1_data_out_2), .MEMORY_ENABLE_2(memory_1_memory_enable_2), .IS_ST_2(memory_1_is_st_2),
    .IS_LD_2(memory_1_is_ld_2), .DATA_IN_2(memory_1_data_in_2), .DATA_OUT(memory_1_data_out));
  LED MEMORY_ENABLE (.in(memory_1_memory_enable_2));
  LED IS_ST (.in(memory_1_is_st_2));
  LED IS_LD (.in(memory_1_is_ld_2));
  // Probe on memory_1_address_2
  // Probe on memory_1_data_in_2
  // Probe on memory_1_data_out

  // Notes on the sheet:
  //   sayfayı büyültmek için 
endmodule

module DLATCH (
  input  D,
  input  CLCK,
  output Q
);

  wire and_1_out, and_2_out, nor_1_out;

  and and_1 (and_1_out, D, CLCK);
  and and_2 (and_2_out, CLCK, ~D);  // AND_Gate
  nor nor_1 (nor_1_out, and_1_out, Q);
  nor nor_2 (Q, nor_1_out, and_2_out);
endmodule

module DFLIP_FLOP (
  input  D,
  input  CLCK,
  output Q
);

  wire master_q, not_1_out;

  not not_1 (not_1_out, CLCK);
  DLATCH master (.D(D), .CLCK(not_1_out), .Q(master_q));
  DLATCH servant (.D(master_q), .CLCK(CLCK), .Q(Q));
endmodule

// IR
module _18BIT_REGISTER (
  input  [17:0] \input ,
  input  RESET,
  input  E,
  input  CLCK,
  output [17:0] out_5
);

  wire multiplexer_1_out, multiplexer_2_out, multiplexer_3_out, multiplexer_4_out, multiplexer_5_out,
       multiplexer_6_out, multiplexer_7_out, multiplexer_8_out, multiplexer_9_out, multiplexer_10_out,
       multiplexer_11_out, multiplexer_12_out, multiplexer_13_out, multiplexer_14_out, multiplexer_15_out,
       multiplexer_16_out, multiplexer_17_out, multiplexer_18_out, multiplexer_19_out, multiplexer_20_out,
       multiplexer_21_out, multiplexer_22_out, multiplexer_23_out, multiplexer_24_out, multiplexer_25_out,
       multiplexer_26_out, multiplexer_27_out, multiplexer_28_out, multiplexer_29_out, multiplexer_30_out,
       multiplexer_31_out, multiplexer_32_out, multiplexer_33_out, multiplexer_34_out, multiplexer_35_out,
       multiplexer_36_out, nor_1_out;

  nor nor_1 (nor_1_out, RESET, E);
  Multiplexer #(.enable("false")) multiplexer_1 (.in0(\input [17]), .in1(1'b0), .out(multiplexer_1_out), .sel(RESET));
  Multiplexer #(.enable("false")) multiplexer_2 (
    .in0(multiplexer_1_out), .in1(out_5[17]), .out(multiplexer_2_out), .sel(nor_1_out));
  Multiplexer #(.enable("false")) multiplexer_3 (.in0(\input [16]), .in1(1'b0), .out(multiplexer_3_out), .sel(RESET));
  Multiplexer #(.enable("false")) multiplexer_4 (
    .in0(multiplexer_3_out), .in1(out_5[16]), .out(multiplexer_4_out), .sel(nor_1_out));
  DFLIP_FLOP dflip_flop_1 (.D(multiplexer_2_out), .CLCK(CLCK), .Q(out_5[17]));
  Multiplexer #(.enable("false")) multiplexer_5 (.in0(\input [15]), .in1(1'b0), .out(multiplexer_5_out), .sel(RESET));
  Multiplexer #(.enable("false")) multiplexer_6 (
    .in0(multiplexer_5_out), .in1(out_5[15]), .out(multiplexer_6_out), .sel(nor_1_out));
  DFLIP_FLOP i (.D(multiplexer_4_out), .CLCK(CLCK), .Q(out_5[16]));
  DFLIP_FLOP dflip_flop_2 (.D(multiplexer_6_out), .CLCK(CLCK), .Q(out_5[15]));
  Multiplexer #(.enable("false")) multiplexer_7 (.in0(\input [14]), .in1(1'b0), .out(multiplexer_7_out), .sel(RESET));
  Multiplexer #(.enable("false")) multiplexer_8 (
    .in0(multiplexer_7_out), .in1(out_5[14]), .out(multiplexer_8_out), .sel(nor_1_out));
  DFLIP_FLOP dflip_flop_3 (.D(multiplexer_8_out), .CLCK(CLCK), .Q(out_5[14]));
  Multiplexer #(.enable("false")) multiplexer_9 (.in0(\input [12]), .in1(1'b0), .out(multiplexer_9_out), .sel(RESET));
  Multiplexer #(.enable("false")) multiplexer_10 (.in0(\input [13]), .in1(1'b0), .out(multiplexer_10_out), .sel(RESET));
  Multiplexer #(.enable("false")) multiplexer_11 (
    .in0(multiplexer_10_out), .in1(out_5[13]), .out(multiplexer_11_out), .sel(nor_1_out));
  DFLIP_FLOP dflip_flop_4 (.D(multiplexer_11_out), .CLCK(CLCK), .Q(out_5[13]));
  Multiplexer #(.enable("false")) multiplexer_12 (.in0(\input [11]), .in1(1'b0), .out(multiplexer_12_out), .sel(RESET));
  Multiplexer #(.enable("false")) multiplexer_13 (
    .in0(multiplexer_9_out), .in1(out_5[12]), .out(multiplexer_13_out), .sel(nor_1_out));
  DFLIP_FLOP dflip_flop_5 (.D(multiplexer_13_out), .CLCK(CLCK), .Q(out_5[12]));
  Multiplexer #(.enable("false")) multiplexer_14 (.in0(\input [10]), .in1(1'b0), .out(multiplexer_14_out), .sel(RESET));
  Multiplexer #(.enable("false")) multiplexer_15 (
    .in0(multiplexer_12_out), .in1(out_5[11]), .out(multiplexer_15_out), .sel(nor_1_out));
  Multiplexer #(.enable("false")) multiplexer_16 (
    .in0(multiplexer_14_out), .in1(out_5[10]), .out(multiplexer_16_out), .sel(nor_1_out));
  DFLIP_FLOP dflip_flop_6 (.D(multiplexer_15_out), .CLCK(CLCK), .Q(out_5[11]));
  Multiplexer #(.enable("false")) multiplexer_17 (.in0(\input [9]), .in1(1'b0), .out(multiplexer_17_out), .sel(RESET));
  Multiplexer #(.enable("false")) multiplexer_18 (
    .in0(multiplexer_17_out), .in1(out_5[9]), .out(multiplexer_18_out), .sel(nor_1_out));
  DFLIP_FLOP dflip_flop_7 (.D(multiplexer_16_out), .CLCK(CLCK), .Q(out_5[10]));
  Multiplexer #(.enable("false")) multiplexer_19 (.in0(\input [8]), .in1(1'b0), .out(multiplexer_19_out), .sel(RESET));
  Multiplexer #(.enable("false")) multiplexer_20 (
    .in0(multiplexer_19_out), .in1(out_5[8]), .out(multiplexer_20_out), .sel(nor_1_out));
  DFLIP_FLOP dflip_flop_8 (.D(multiplexer_18_out), .CLCK(CLCK), .Q(out_5[9]));
  Multiplexer #(.enable("false")) multiplexer_21 (.in0(\input [7]), .in1(1'b0), .out(multiplexer_21_out), .sel(RESET));
  Multiplexer #(.enable("false")) multiplexer_22 (
    .in0(multiplexer_21_out), .in1(out_5[7]), .out(multiplexer_22_out), .sel(nor_1_out));
  DFLIP_FLOP dflip_flop_9 (.D(multiplexer_20_out), .CLCK(CLCK), .Q(out_5[8]));
  DFLIP_FLOP dflip_flop_10 (.D(multiplexer_22_out), .CLCK(CLCK), .Q(out_5[7]));
  Multiplexer #(.enable("false")) multiplexer_23 (.in0(\input [6]), .in1(1'b0), .out(multiplexer_23_out), .sel(RESET));
  Multiplexer #(.enable("false")) multiplexer_24 (
    .in0(multiplexer_23_out), .in1(out_5[6]), .out(multiplexer_24_out), .sel(nor_1_out));
  DFLIP_FLOP dflip_flop_11 (.D(multiplexer_24_out), .CLCK(CLCK), .Q(out_5[6]));
  Multiplexer #(.enable("false")) multiplexer_25 (.in0(\input [4]), .in1(1'b0), .out(multiplexer_25_out), .sel(RESET));
  Multiplexer #(.enable("false")) multiplexer_26 (.in0(\input [5]), .in1(1'b0), .out(multiplexer_26_out), .sel(RESET));
  Multiplexer #(.enable("false")) multiplexer_27 (
    .in0(multiplexer_26_out), .in1(out_5[5]), .out(multiplexer_27_out), .sel(nor_1_out));
  DFLIP_FLOP dflip_flop_12 (.D(multiplexer_27_out), .CLCK(CLCK), .Q(out_5[5]));
  Multiplexer #(.enable("false")) multiplexer_28 (.in0(\input [3]), .in1(1'b0), .out(multiplexer_28_out), .sel(RESET));
  Multiplexer #(.enable("false")) multiplexer_29 (
    .in0(multiplexer_25_out), .in1(out_5[4]), .out(multiplexer_29_out), .sel(nor_1_out));
  DFLIP_FLOP dflip_flop_13 (.D(multiplexer_29_out), .CLCK(CLCK), .Q(out_5[4]));
  Multiplexer #(.enable("false")) multiplexer_30 (.in0(\input [2]), .in1(1'b0), .out(multiplexer_30_out), .sel(RESET));
  Multiplexer #(.enable("false")) multiplexer_31 (
    .in0(multiplexer_28_out), .in1(out_5[3]), .out(multiplexer_31_out), .sel(nor_1_out));
  Multiplexer #(.enable("false")) multiplexer_32 (
    .in0(multiplexer_30_out), .in1(out_5[2]), .out(multiplexer_32_out), .sel(nor_1_out));
  DFLIP_FLOP dflip_flop_14 (.D(multiplexer_31_out), .CLCK(CLCK), .Q(out_5[3]));
  Multiplexer #(.enable("false")) multiplexer_33 (.in0(\input [1]), .in1(1'b0), .out(multiplexer_33_out), .sel(RESET));
  Multiplexer #(.enable("false")) multiplexer_34 (
    .in0(multiplexer_33_out), .in1(out_5[1]), .out(multiplexer_34_out), .sel(nor_1_out));
  DFLIP_FLOP dflip_flop_15 (.D(multiplexer_32_out), .CLCK(CLCK), .Q(out_5[2]));
  Multiplexer #(.enable("false")) multiplexer_35 (.in0(\input [0]), .in1(1'b0), .out(multiplexer_35_out), .sel(RESET));
  Multiplexer #(.enable("false")) multiplexer_36 (
    .in0(multiplexer_35_out), .in1(out_5[0]), .out(multiplexer_36_out), .sel(nor_1_out));
  DFLIP_FLOP dflip_flop_16 (.D(multiplexer_34_out), .CLCK(CLCK), .Q(out_5[1]));
  DFLIP_FLOP dflip_flop_17 (.D(multiplexer_36_out), .CLCK(CLCK), .Q(out_5[0]));
endmodule

module REGISTER_FILE (
  input  CLCK,
  input  RESET_ENABLE,
  input  [17:0] DATA,
  input  [3:0] REG_1,
  input  WRITE_ENABLE,
  input  [3:0] REG_2,
  input  [3:0] SELECT_REGISTER,
  output [17:0] DATA_2,
  output [17:0] READ_REG_1_VALUE,
  output [17:0] READ_REG_1_VALUE_2,
  output WRITE_ENABLE_2,
  output [17:0] READ_REG_2_VALUE,
  output [17:0] READ_REG_2_VALUE_2,
  output [3:0] DESTINATION
);

  wire and_1_out, and_2_out, and_3_out, and_4_out, and_5_out, and_6_out, and_7_out, and_8_out, and_9_out,
       and_10_out, and_11_out, and_12_out, and_13_out, and_14_out, and_15_out, and_16_out, decoder_1_out0,
       decoder_1_out1, decoder_1_out2, decoder_1_out3, decoder_1_out4, decoder_1_out5, decoder_1_out6,
       decoder_1_out7, decoder_1_out8, decoder_1_out9, decoder_1_out10, decoder_1_out11, decoder_1_out12,
       decoder_1_out13, decoder_1_out14, decoder_1_out15;
  wire [17:0] R0_out_5, R1_out_5, R2_out_5, R3_out_5, R4_out_5, R5_out_5, R6_out_5, R7_out_5, R8_out_5,
       R9_out_5, R10_out_5, R11_out_5, R12_out_5, R13_out_5, R14_out_5, R15_out_5;

  Decoder #(.select(4), .enable("false")) decoder_1 (
    .out0(decoder_1_out0), .out1(decoder_1_out1), .out2(decoder_1_out2), .out3(decoder_1_out3),
    .out4(decoder_1_out4), .out5(decoder_1_out5), .out6(decoder_1_out6), .out7(decoder_1_out7),
    .out8(decoder_1_out8), .out9(decoder_1_out9), .out10(decoder_1_out10), .out11(decoder_1_out11),
    .out12(decoder_1_out12), .out13(decoder_1_out13), .out14(decoder_1_out14), .out15(decoder_1_out15),
    .sel(SELECT_REGISTER));
  and and_1 (and_1_out, decoder_1_out15, WRITE_ENABLE);
  and and_2 (and_2_out, decoder_1_out14, WRITE_ENABLE);
  and and_3 (and_3_out, decoder_1_out13, WRITE_ENABLE);
  and and_4 (and_4_out, decoder_1_out12, WRITE_ENABLE);
  and and_5 (and_5_out, decoder_1_out11, WRITE_ENABLE);
  and and_6 (and_6_out, decoder_1_out10, WRITE_ENABLE);
  and and_7 (and_7_out, decoder_1_out9, WRITE_ENABLE);
  and and_8 (and_8_out, decoder_1_out8, WRITE_ENABLE);
  and and_9 (and_9_out, decoder_1_out7, WRITE_ENABLE);
  and and_10 (and_10_out, decoder_1_out6, WRITE_ENABLE);
  and and_11 (and_11_out, decoder_1_out5, WRITE_ENABLE);
  and and_12 (and_12_out, decoder_1_out4, WRITE_ENABLE);
  and and_13 (and_13_out, decoder_1_out3, WRITE_ENABLE);
  and and_14 (and_14_out, decoder_1_out2, WRITE_ENABLE);
  and and_15 (and_15_out, decoder_1_out1, WRITE_ENABLE);
  and and_16 (and_16_out, decoder_1_out0, WRITE_ENABLE);
  _18BIT_REGISTER R15 (.\input (DATA), .CLCK(CLCK), .out_5(R15_out_5), .RESET(RESET_ENABLE), .E(and_1_out));
  _18BIT_REGISTER R14 (.\input (DATA), .CLCK(CLCK), .out_5(R14_out_5), .RESET(RESET_ENABLE), .E(and_2_out));
  _18BIT_REGISTER R13 (.\input (DATA), .CLCK(CLCK), .out_5(R13_out_5), .RESET(RESET_ENABLE), .E(and_3_out));
  _18BIT_REGISTER R12 (.\input (DATA), .CLCK(CLCK), .out_5(R12_out_5), .RESET(RESET_ENABLE), .E(and_4_out));
  _18BIT_REGISTER R11 (.\input (DATA), .CLCK(CLCK), .out_5(R11_out_5), .RESET(RESET_ENABLE), .E(and_5_out));
  _18BIT_REGISTER R10 (.\input (DATA), .CLCK(CLCK), .out_5(R10_out_5), .RESET(RESET_ENABLE), .E(and_6_out));
  _18BIT_REGISTER R9 (.\input (DATA), .CLCK(CLCK), .out_5(R9_out_5), .RESET(RESET_ENABLE), .E(and_7_out));
  _18BIT_REGISTER R8 (.\input (DATA), .CLCK(CLCK), .out_5(R8_out_5), .RESET(RESET_ENABLE), .E(and_8_out));
  _18BIT_REGISTER R7 (.\input (DATA), .CLCK(CLCK), .out_5(R7_out_5), .RESET(RESET_ENABLE), .E(and_9_out));
  _18BIT_REGISTER R6 (.\input (DATA), .CLCK(CLCK), .out_5(R6_out_5), .RESET(RESET_ENABLE), .E(and_10_out));
  _18BIT_REGISTER R5 (.\input (DATA), .CLCK(CLCK), .out_5(R5_out_5), .RESET(RESET_ENABLE), .E(and_11_out));
  _18BIT_REGISTER R4 (.\input (DATA), .CLCK(CLCK), .out_5(R4_out_5), .RESET(RESET_ENABLE), .E(and_12_out));
  _18BIT_REGISTER R3 (.\input (DATA), .CLCK(CLCK), .out_5(R3_out_5), .RESET(RESET_ENABLE), .E(and_13_out));
  _18BIT_REGISTER R2 (.\input (DATA), .CLCK(CLCK), .out_5(R2_out_5), .RESET(RESET_ENABLE), .E(and_14_out));
  _18BIT_REGISTER R1 (.\input (DATA), .CLCK(CLCK), .out_5(R1_out_5), .RESET(RESET_ENABLE), .E(and_15_out));
  _18BIT_REGISTER R0 (.\input (DATA), .CLCK(CLCK), .out_5(R0_out_5), .RESET(RESET_ENABLE), .E(and_16_out));
  Multiplexer #(.select(4), .width(18), .enable("false")) multiplexer_1 (
    .in0(R0_out_5), .in1(R1_out_5), .in2(R2_out_5), .in3(R3_out_5), .in4(R4_out_5), .in5(R5_out_5),
    .in6(R6_out_5), .in7(R7_out_5), .in8(R8_out_5), .in9(R9_out_5), .in10(R10_out_5), .in11(R11_out_5),
    .in12(R12_out_5), .in13(R13_out_5), .in14(R14_out_5), .in15(R15_out_5), .out(READ_REG_1_VALUE),
    .sel(REG_1));
  Multiplexer #(.select(4), .width(18), .enable("false")) multiplexer_2 (
    .in0(R0_out_5), .in1(R1_out_5), .in2(R2_out_5), .in3(R3_out_5), .in4(R4_out_5), .in5(R5_out_5),
    .in6(R6_out_5), .in7(R7_out_5), .in8(R8_out_5), .in9(R9_out_5), .in10(R10_out_5), .in11(R11_out_5),
    .in12(R12_out_5), .in13(R13_out_5), .in14(R14_out_5), .in15(R15_out_5), .out(READ_REG_2_VALUE),
    .sel(REG_2));

  assign DATA_2 = DATA;
  assign DESTINATION = SELECT_REGISTER;
  assign READ_REG_1_VALUE_2 = READ_REG_1_VALUE;
  assign READ_REG_2_VALUE_2 = READ_REG_2_VALUE;
  assign WRITE_ENABLE_2 = WRITE_ENABLE;
endmodule

module AND (
  input  [17:0] R1,
  input  [17:0] R2,
  output [17:0] Q
);

  assign Q = R1 & R2;  // AND_Gate and_1, 18 bits wide
endmodule

module NAND (
  input  [17:0] R1,
  input  [17:0] R2,
  output [17:0] Q
);

  assign Q = ~(R1 & R2);  // NAND_Gate nand_1, 18 bits wide
endmodule

module NOR (
  input  [17:0] R1,
  input  [17:0] R2,
  output [17:0] Q
);

  assign Q = ~(R1 | R2);  // NOR_Gate nor_1, 18 bits wide
endmodule

module ADD (
  input  [17:0] BIT_1,
  input  [17:0] BIT_2,
  input  C_IN,
  output [17:0] out_4,
  output C_OUT
);

  wire add_16_bit_1_c_out;

  ADD_16_BIT add_16_bit_1 (
    .BIT_1(BIT_1[15:0]), .BIT_2(BIT_2[15:0]), .C_IN(C_IN), .out_4(out_4[15:0]), .C_OUT(add_16_bit_1_c_out));
  ADD_2_BIT add_2_bit_1 (
    .BIT_1(BIT_1[17:16]), .BIT_2(BIT_2[17:16]), .C_IN(add_16_bit_1_c_out), .out_4(out_4[17:16]), .C_OUT(C_OUT));
endmodule

module ADD_16_BIT (
  input  [15:0] BIT_1,
  input  [15:0] BIT_2,
  input  C_IN,
  output [15:0] out_4,
  output C_OUT
);

  wire add_8_bit_1_c_out;

  ADD_8_BIT add_8_bit_1 (
    .BIT_1(BIT_1[7:0]), .BIT_2(BIT_2[7:0]), .C_IN(C_IN), .out_4(out_4[7:0]), .C_OUT(add_8_bit_1_c_out));
  ADD_8_BIT add_8_bit_2 (
    .BIT_1(BIT_1[15:8]), .BIT_2(BIT_2[15:8]), .C_IN(add_8_bit_1_c_out), .out_4(out_4[15:8]), .C_OUT(C_OUT));
endmodule

module ADD_8_BIT (
  input  [7:0] BIT_1,
  input  [7:0] BIT_2,
  input  C_IN,
  output [7:0] out_4,
  output C_OUT
);

  wire add_4_bit_1_c_out;

  ADD_4_BIT add_4_bit_1 (
    .BIT_1(BIT_1[3:0]), .BIT_2(BIT_2[3:0]), .C_IN(C_IN), .out_4(out_4[3:0]), .C_OUT(add_4_bit_1_c_out));
  ADD_4_BIT add_4_bit_2 (
    .BIT_1(BIT_1[7:4]), .BIT_2(BIT_2[7:4]), .C_IN(add_4_bit_1_c_out), .out_4(out_4[7:4]), .C_OUT(C_OUT));
endmodule

module ADD_4_BIT (
  input  [3:0] BIT_1,
  input  [3:0] BIT_2,
  input  C_IN,
  output [3:0] out_4,
  output C_OUT
);

  wire add_2_bit_1_c_out;

  ADD_2_BIT add_2_bit_1 (
    .BIT_1(BIT_1[1:0]), .BIT_2(BIT_2[1:0]), .C_IN(C_IN), .out_4(out_4[1:0]), .C_OUT(add_2_bit_1_c_out));
  ADD_2_BIT add_2_bit_2 (
    .BIT_1(BIT_1[3:2]), .BIT_2(BIT_2[3:2]), .C_IN(add_2_bit_1_c_out), .out_4(out_4[3:2]), .C_OUT(C_OUT));
endmodule

module ADD_2_BIT (
  input  [1:0] BIT_1,
  input  [1:0] BIT_2,
  input  C_IN,
  output [1:0] out_4,
  output C_OUT
);

  wire add_1_bit_1_c_out;

  ADD_1_BIT add_1_bit_1 (.BIT_1(BIT_1[0]), .BIT_2(BIT_2[0]), .C_IN(C_IN), .SUM(out_4[0]), .C_OUT(add_1_bit_1_c_out));
  ADD_1_BIT add_1_bit_2 (.BIT_1(BIT_1[1]), .BIT_2(BIT_2[1]), .C_IN(add_1_bit_1_c_out), .SUM(out_4[1]), .C_OUT(C_OUT));
endmodule

module ADD_1_BIT (
  input  BIT_1,
  input  BIT_2,
  input  C_IN,
  output SUM,
  output C_OUT
);

  wire and_1_out, and_2_out, xor_1_out;

  xor xor_1 (xor_1_out, BIT_1, BIT_2);
  xor xor_2 (SUM, xor_1_out, C_IN);
  and and_1 (and_1_out, xor_1_out, C_IN);
  and and_2 (and_2_out, BIT_2, BIT_1);
  or or_1 (C_OUT, and_1_out, and_2_out);
endmodule

module CMP (
  input  [17:0] OP1,
  input  [17:0] OP2,
  input  CLCK,
  input  IS_CMP,
  input  RESET,
  output [17:0] OP1_2,
  output CF,
  output [17:0] OP2_2,
  output CF_LED,
  output ZF,
  output ZF_LED,
  output IS_CMP_2
);

  wire and_1_out, and_2_out, and_3_out, and_4_out, and_5_out, and_6_out, and_7_out, and_8_out,
       multiplexer_1_out, multiplexer_2_out;
  wire [16:0] xnor_2_out;
  wire [17:0] add_1_out_4, add_2_out_4, not_1_out, xnor_1_out;

  assign not_1_out = ~OP2;  // NOT_Gate not_1, 18 bits wide
  ADD add_1 (.BIT_1(not_1_out), .BIT_2(18'h1), .C_IN(1'b0), .out_4(add_1_out_4));  // open: C_OUT
  ADD add_2 (.BIT_1(add_1_out_4), .BIT_2(OP1), .C_IN(1'b0), .out_4(add_2_out_4));  // open: C_OUT
  assign xnor_1_out = ~(OP1 ^ OP2);  // XNOR_Gate xnor_1, 18 bits wide
  and and_1 (and_1_out, xnor_1_out[0], xnor_1_out[1], xnor_1_out[2], xnor_1_out[3], xnor_1_out[4], xnor_1_out[5], xnor_1_out[6], xnor_1_out[7], xnor_1_out[8], xnor_1_out[10], xnor_1_out[11], xnor_1_out[12], xnor_1_out[13], xnor_1_out[14], xnor_1_out[15], xnor_1_out[16], xnor_1_out[17], xnor_1_out[9]);
  and and_2 (and_2_out, add_2_out_4[17], ~and_5_out);  // AND_Gate
  and and_3 (and_3_out, ~and_1_out, ~and_2_out);  // AND_Gate
  and and_4 (and_4_out, ~and_1_out, and_2_out);  // AND_Gate
  and and_5 (and_5_out, xnor_2_out[0], xnor_2_out[1], xnor_2_out[2], xnor_2_out[3], xnor_2_out[4], xnor_2_out[5], xnor_2_out[6], xnor_2_out[7], xnor_2_out[8], xnor_2_out[9], xnor_2_out[10], xnor_2_out[11], xnor_2_out[12], xnor_2_out[13], xnor_2_out[14], xnor_2_out[15], xnor_2_out[16]);
  assign xnor_2_out = ~(add_2_out_4[16:0] ^ {17{1'b0}});  // XNOR_Gate xnor_2, 17 bits wide
  and and_6 (and_6_out, and_1_out, ~and_3_out, ~and_4_out);  // AND_Gate
  and and_7 (and_7_out, ~and_1_out, ~and_3_out, and_4_out);  // AND_Gate
  and and_8 (and_8_out, CLCK, IS_CMP);
  Multiplexer #(.enable("false")) multiplexer_1 (.in0(and_7_out), .in1(1'b0), .out(multiplexer_1_out), .sel(RESET));
  DFLIP_FLOP dflip_flop_1 (.D(multiplexer_1_out), .CLCK(and_8_out), .Q(CF));
  Multiplexer #(.enable("false")) multiplexer_2 (.in0(and_6_out), .in1(1'b0), .out(multiplexer_2_out), .sel(RESET));
  DFLIP_FLOP dflip_flop_2 (.D(multiplexer_2_out), .CLCK(and_8_out), .Q(ZF));

  assign CF_LED = CF;
  assign IS_CMP_2 = IS_CMP;
  assign OP1_2 = OP1;
  assign OP2_2 = OP2;
  assign ZF_LED = ZF;

  // Notes on the sheet:
  //   eşit durumu
  //   zf = 1, cf = 0 olmalı
  //   r1>r2
  //   r1=r2
  //   r1<r2
endmodule

module ADD_10_BIT (
  input  [9:0] BIT_1,
  input  [9:0] BIT_2,
  input  C_IN,
  output [9:0] out_4,
  output C_OUT
);

  wire add_8_bit_1_c_out;

  ADD_8_BIT add_8_bit_1 (
    .BIT_1(BIT_1[7:0]), .BIT_2(BIT_2[7:0]), .C_IN(C_IN), .out_4(out_4[7:0]), .C_OUT(add_8_bit_1_c_out));
  ADD_2_BIT add_2_bit_1 (
    .BIT_1(BIT_1[9:8]), .BIT_2(BIT_2[9:8]), .C_IN(add_8_bit_1_c_out), .out_4(out_4[9:8]), .C_OUT(C_OUT));
endmodule

module _10BIT_REGISTER (
  input  [9:0] \input ,
  input  RESET,
  input  E,
  input  CLCK,
  output [9:0] out_5
);

  wire multiplexer_1_out, multiplexer_2_out, multiplexer_3_out, multiplexer_4_out, multiplexer_5_out,
       multiplexer_6_out, multiplexer_7_out, multiplexer_8_out, multiplexer_9_out, multiplexer_10_out,
       multiplexer_11_out, multiplexer_12_out, multiplexer_13_out, multiplexer_14_out, multiplexer_15_out,
       multiplexer_16_out, multiplexer_17_out, multiplexer_18_out, multiplexer_19_out, multiplexer_20_out,
       not_1_out;

  not not_1 (not_1_out, E);
  Multiplexer #(.enable("false")) multiplexer_1 (.in0(\input [9]), .in1(1'b0), .out(multiplexer_1_out), .sel(RESET));
  Multiplexer #(.enable("false")) multiplexer_2 (
    .in0(multiplexer_1_out), .in1(out_5[9]), .out(multiplexer_2_out), .sel(not_1_out));
  DFLIP_FLOP dflip_flop_1 (.D(multiplexer_2_out), .CLCK(CLCK), .Q(out_5[9]));
  Multiplexer #(.enable("false")) multiplexer_3 (.in0(\input [7]), .in1(1'b0), .out(multiplexer_3_out), .sel(RESET));
  Multiplexer #(.enable("false")) multiplexer_4 (.in0(\input [8]), .in1(1'b0), .out(multiplexer_4_out), .sel(RESET));
  Multiplexer #(.enable("false")) multiplexer_5 (
    .in0(multiplexer_4_out), .in1(out_5[8]), .out(multiplexer_5_out), .sel(not_1_out));
  DFLIP_FLOP dflip_flop_2 (.D(multiplexer_5_out), .CLCK(CLCK), .Q(out_5[8]));
  Multiplexer #(.enable("false")) multiplexer_6 (.in0(\input [6]), .in1(1'b0), .out(multiplexer_6_out), .sel(RESET));
  Multiplexer #(.enable("false")) multiplexer_7 (
    .in0(multiplexer_3_out), .in1(out_5[7]), .out(multiplexer_7_out), .sel(not_1_out));
  DFLIP_FLOP dflip_flop_3 (.D(multiplexer_7_out), .CLCK(CLCK), .Q(out_5[7]));
  Multiplexer #(.enable("false")) multiplexer_8 (.in0(\input [5]), .in1(1'b0), .out(multiplexer_8_out), .sel(RESET));
  Multiplexer #(.enable("false")) multiplexer_9 (
    .in0(multiplexer_6_out), .in1(out_5[6]), .out(multiplexer_9_out), .sel(not_1_out));
  Multiplexer #(.enable("false")) multiplexer_10 (
    .in0(multiplexer_8_out), .in1(out_5[5]), .out(multiplexer_10_out), .sel(not_1_out));
  DFLIP_FLOP dflip_flop_4 (.D(multiplexer_9_out), .CLCK(CLCK), .Q(out_5[6]));
  Multiplexer #(.enable("false")) multiplexer_11 (.in0(\input [4]), .in1(1'b0), .out(multiplexer_11_out), .sel(RESET));
  Multiplexer #(.enable("false")) multiplexer_12 (
    .in0(multiplexer_11_out), .in1(out_5[4]), .out(multiplexer_12_out), .sel(not_1_out));
  DFLIP_FLOP dflip_flop_5 (.D(multiplexer_10_out), .CLCK(CLCK), .Q(out_5[5]));
  Multiplexer #(.enable("false")) multiplexer_13 (.in0(\input [3]), .in1(1'b0), .out(multiplexer_13_out), .sel(RESET));
  Multiplexer #(.enable("false")) multiplexer_14 (
    .in0(multiplexer_13_out), .in1(out_5[3]), .out(multiplexer_14_out), .sel(not_1_out));
  DFLIP_FLOP dflip_flop_6 (.D(multiplexer_12_out), .CLCK(CLCK), .Q(out_5[4]));
  Multiplexer #(.enable("false")) multiplexer_15 (.in0(\input [2]), .in1(1'b0), .out(multiplexer_15_out), .sel(RESET));
  Multiplexer #(.enable("false")) multiplexer_16 (
    .in0(multiplexer_15_out), .in1(out_5[2]), .out(multiplexer_16_out), .sel(not_1_out));
  DFLIP_FLOP dflip_flop_7 (.D(multiplexer_14_out), .CLCK(CLCK), .Q(out_5[3]));
  DFLIP_FLOP dflip_flop_8 (.D(multiplexer_16_out), .CLCK(CLCK), .Q(out_5[2]));
  Multiplexer #(.enable("false")) multiplexer_17 (.in0(\input [1]), .in1(1'b0), .out(multiplexer_17_out), .sel(RESET));
  Multiplexer #(.enable("false")) multiplexer_18 (
    .in0(multiplexer_17_out), .in1(out_5[1]), .out(multiplexer_18_out), .sel(not_1_out));
  DFLIP_FLOP dflip_flop_9 (.D(multiplexer_18_out), .CLCK(CLCK), .Q(out_5[1]));
  Multiplexer #(.enable("false")) multiplexer_19 (.in0(\input [0]), .in1(1'b0), .out(multiplexer_19_out), .sel(RESET));
  Multiplexer #(.enable("false")) multiplexer_20 (
    .in0(multiplexer_19_out), .in1(out_5[0]), .out(multiplexer_20_out), .sel(not_1_out));
  DFLIP_FLOP dflip_flop_10 (.D(multiplexer_20_out), .CLCK(CLCK), .Q(out_5[0]));
endmodule

module ALU (
  input  IS_IMM,
  input  IS_ALU,
  input  [17:0] R1,
  input  [17:0] R2,
  input  [1:0] ALU_OPR_TYPE,
  output IS_IMM_LED,
  output IS_ALU_LED,
  output [17:0] ALU_R1,
  output [17:0] ALU_R2,
  output [17:0] RESULT,
  output NOR,
  output NAND,
  output AND,
  output ADD,
  output [17:0] RESULT_2
);

  wire [17:0] add_1_out_4, and_1_q, nand_1_q, nor_1_q;

  Multiplexer #(.select(2), .width(18), .enable("false")) multiplexer_1 (
    .in0(add_1_out_4), .in1(and_1_q), .in2(nand_1_q), .in3(nor_1_q), .out(RESULT), .sel(ALU_OPR_TYPE));
  ADD add_1 (.BIT_1(R2), .BIT_2(R1), .C_IN(1'b0), .out_4(add_1_out_4));  // open: C_OUT
  AND and_1 (.R1(R2), .R2(R1), .Q(and_1_q));
  NAND nand_1 (.R1(R2), .R2(R1), .Q(nand_1_q));
  NOR nor_1 (.R1(R2), .R2(R1), .Q(nor_1_q));
  Decoder #(.select(2)) decoder_1 (.out0(ADD), .out1(AND), .out2(NAND), .out3(NOR), .sel(ALU_OPR_TYPE), .en(IS_ALU));

  assign ALU_R1 = R1;
  assign ALU_R2 = R2;
  assign IS_ALU_LED = IS_ALU;
  assign IS_IMM_LED = IS_IMM;
  assign RESULT_2 = RESULT;
endmodule

module PC (
  input  IS_JUMP,
  input  [9:0] ADDRESS,
  input  RESET,
  input  PC_ENABLE,
  input  NEXT,
  input  CLCK,
  output IS_JUMP_2,
  output [9:0] CURRENT_ADDRESS,
  output [9:0] CURRENT_ADDRESS_2,
  output PC_ENABLE_2
);

  wire and_1_out, not_1_out;
  wire [9:0] add_10_bit_1_out_4;

  ADD_10_BIT add_10_bit_1 (
    .BIT_1(CURRENT_ADDRESS), .BIT_2(ADDRESS), .C_IN(1'b0), .out_4(add_10_bit_1_out_4));  // open: C_OUT
  and and_1 (and_1_out, PC_ENABLE, NEXT, CLCK);
  Counter #(.width(10), .max('h3ff), .ongoal("continue")) counter_1 (
    .load(IS_JUMP), .D(add_10_bit_1_out_4), .count(not_1_out), .Q(CURRENT_ADDRESS), .clk(and_1_out),
    .clr(RESET));  // open: carry
  not not_1 (not_1_out, IS_JUMP);

  assign CURRENT_ADDRESS_2 = CURRENT_ADDRESS;
  assign IS_JUMP_2 = IS_JUMP;
  assign PC_ENABLE_2 = PC_ENABLE;
endmodule

module SIGNEXTENSION (
  input  [5:0] INPUT,
  output [17:0] EXTENDED
);

  Multiplexer #(.width(12), .enable("false")) multiplexer_1 (
    .in0({12{1'b0}}), .in1({12{1'b1}}), .out(EXTENDED[17:6]), .sel(INPUT[5]));

  assign EXTENDED[5:0] = INPUT;
endmodule

module CU (
  input  CLOCK,
  input  [17:0] IR_VALUE,
  input  [17:0] SRC1_VALUE,
  input  [17:0] SRC2_VALUE,
  input  [17:0] ALU_RESULT_VALUE,
  input  [17:0] VALUE_FROM_RAM,
  input  RESET_MANUEL,
  input  ZF,
  input  CF,
  output CLOCK_REGFILE,
  output CLOCK_PC,
  output CLOCK_MEMORY,
  output CLOCK_CMP,
  output IS_ALU,
  output NEXT_INS,
  output NEXT_INS_LED,
  output [3:0] READ_REG1,
  output IS_WRITE_REGFILE,
  output [3:0] READ_REG2,
  output PC_ENABLE,
  output [9:0] ADDRESS,
  output MEMORY_ENABLE,
  output IS_LD,
  output IS_ST,
  output [3:0] DST_SRC,
  output IS_JUMP,
  output [17:0] DATA_TO_REG_FILE,
  output IS_CMP,
  output RESET_PC,
  output IS_IMM,
  output IS_RESET_REGFILE,
  output [17:0] ALU_R1,
  output IS_RESET_LED,
  output IS_RESET_CMP,
  output [17:0] ALU_R2,
  output [1:0] ALU_OPR_TYPE,
  output [9:0] RAM_ADDRESS,
  output [17:0] RAM_DATA,
  output [17:0] OP1,
  output [17:0] OP2
);

  wire add, addi, \and , and_1_out, and_2_out, and_3_out, and_4_out, and_5_out, and_6_out, andi,
       controlled_buffer_1_out, controlled_buffer_2_out, controlled_buffer_3_out, controlled_buffer_4_out,
       controlled_buffer_5_out, controlled_buffer_6_out, controlled_buffer_13_out, counter_3_q, counter_6_q,
       decoder_2_out0, decoder_2_out2, decoder_3_out0, decoder_3_out2, decoder_4_out1, decoder_4_out3,
       decoder_5_out0, decoder_5_out3, decoder_6_out0, decoder_6_out1, decoder_7_out0, decoder_7_out1,
       IS_WRITE_REGFILE_ALU, IS_WRITE_REGFILE_LD, ja, jae, jb, jbe, je, jump, MEMORY_ENABLE_ST, \nand ,
       NEXT_INS_ALU, NEXT_INS_CMP, NEXT_INS_LD, NEXT_INS_RESET, \nor , not_1_out, or_1_out, or_6_out,
       PC_ENABLE_JUMP;
  wire [1:0] counter_1_q, counter_2_q, counter_4_q, counter_5_q;
  wire [17:0] EXTENDED_VALUE;

  Multiplexer #(.width(4), .enable("false")) multiplexer_1 (
    .in0(IR_VALUE[9:6]), .in1(IR_VALUE[13:10]), .out(READ_REG1), .sel(IS_ST));
  Multiplexer #(.width(18), .enable("false")) multiplexer_2 (
    .in0(VALUE_FROM_RAM), .in1(ALU_RESULT_VALUE), .out(DATA_TO_REG_FILE), .sel(IS_ALU));
  Multiplexer #(.width(18), .enable("false")) multiplexer_3 (
    .in0(SRC2_VALUE), .in1(EXTENDED_VALUE), .out(ALU_R2), .sel(IS_IMM));
  Decoder #(.select(4)) decoder_1 (
    .out0(add), .out1(\and ), .out2(\nand ), .out3(\nor ), .out4(addi), .out5(andi), .out6(IS_LD),
    .out7(IS_ST), .out8(IS_CMP), .out9(jump), .out10(je), .out11(ja), .out12(jb), .out13(jae), .out14(jbe),
    .out15(IS_RESET_CMP), .sel(IR_VALUE[17:14]));  // open: en
  or or_1 (or_1_out, je, ja, jb, jae, jbe);
  and and_1 (and_1_out, or_1_out, ~IS_JUMP);  // AND_Gate
  or or_2 (IS_ALU, add, \and , \nor , \nand , addi, andi);
  or or_3 (IS_IMM, addi, andi);
  and and_2 (and_2_out, je, ZF, ~CF);  // AND_Gate
  and and_3 (and_3_out, ja, ~ZF, ~CF);  // AND_Gate
  and and_4 (and_4_out, jb, ~ZF, CF);  // AND_Gate
  and and_5 (and_5_out, jae, ~CF);  // AND_Gate
  and and_6 (and_6_out, jbe, ZF, CF);
  or or_4 (NEXT_INS, NEXT_INS_CMP, NEXT_INS_RESET, NEXT_INS_ALU, and_1_out, NEXT_INS_LD, MEMORY_ENABLE_ST);
  or or_5 (IS_JUMP, jump, and_2_out, and_3_out, and_4_out, and_5_out, and_6_out);
  or or_6 (or_6_out, \and , andi);
  SIGNEXTENSION signextension_1 (.INPUT(IR_VALUE[5:0]), .EXTENDED(EXTENDED_VALUE));
  or or_7 (IS_WRITE_REGFILE, IS_WRITE_REGFILE_ALU, IS_WRITE_REGFILE_LD);
  or or_8 (ALU_OPR_TYPE[0], or_6_out, \nor );
  or or_9 (ALU_OPR_TYPE[1], \nand , \nor );
  or or_10 (PC_ENABLE, NEXT_INS_CMP, NEXT_INS_ALU, NEXT_INS_LD, MEMORY_ENABLE_ST, PC_ENABLE_JUMP, NEXT_INS_RESET, and_1_out);
  or or_11 (MEMORY_ENABLE, IS_WRITE_REGFILE_LD, MEMORY_ENABLE_ST);
  assign controlled_buffer_1_out = IS_JUMP ? CLOCK : 1'bz;  // Controlled_Buffer controlled_buffer_1
  assign controlled_buffer_2_out = IS_RESET_CMP ? CLOCK : 1'bz;  // Controlled_Buffer controlled_buffer_2
  Decoder #(.select(2), .enable("false")) decoder_2 (
    .out0(decoder_2_out0), .out1(IS_WRITE_REGFILE_ALU), .out2(decoder_2_out2), .sel(counter_1_q));  // open: out3
  Counter #(.width(2), .max('h2)) counter_1 (
    .Q(counter_1_q), .clk(controlled_buffer_3_out), .clr(IS_RESET_CMP));  // open: load, D, count, carry
  assign controlled_buffer_3_out = IS_ALU ? CLOCK : 1'bz;  // Controlled_Buffer controlled_buffer_3
  Decoder #(.select(2), .enable("false")) decoder_3 (
    .out0(decoder_3_out0), .out1(IS_WRITE_REGFILE_LD), .out2(decoder_3_out2), .sel(counter_2_q));  // open: out3
  Counter #(.width(2), .max('h2)) counter_2 (
    .Q(counter_2_q), .clk(controlled_buffer_4_out), .clr(IS_RESET_CMP));  // open: load, D, count, carry
  assign controlled_buffer_4_out = IS_LD ? CLOCK : 1'bz;  // Controlled_Buffer controlled_buffer_4
  Counter #(.width(1), .max('h1)) counter_3 (
    .Q(counter_3_q), .clk(controlled_buffer_5_out), .clr(IS_RESET_CMP));  // open: load, D, count, carry
  assign controlled_buffer_5_out = IS_ST ? CLOCK : 1'bz;  // Controlled_Buffer controlled_buffer_5
  Decoder #(.select(2), .enable("false")) decoder_4 (
    .out1(decoder_4_out1), .out3(decoder_4_out3), .sel(counter_4_q));  // open: out0, out2
  Counter #(.width(2), .max('h2)) counter_4 (
    .Q(counter_4_q), .clk(controlled_buffer_1_out), .clr(IS_RESET_CMP));  // open: load, D, count, carry
  Decoder #(.select(2), .enable("false")) decoder_5 (
    .out0(decoder_5_out0), .out3(decoder_5_out3), .sel(counter_5_q));  // open: out1, out2
  Counter #(.width(2), .max('h3)) counter_5 (
    .Q(counter_5_q), .clk(controlled_buffer_2_out), .clr(not_1_out));  // open: load, D, count, carry
  not not_1 (not_1_out, IS_RESET_CMP);
  Decoder #(.enable("false")) decoder_6 (.out0(decoder_6_out0), .out1(decoder_6_out1), .sel(counter_6_q));
  Counter #(.width(1), .max('h1)) counter_6 (
    .Q(counter_6_q), .clk(controlled_buffer_6_out), .clr(IS_CMP));  // open: load, D, count, carry
  assign controlled_buffer_6_out = IS_RESET_CMP ? CLOCK : 1'bz;  // Controlled_Buffer controlled_buffer_6
  assign NEXT_INS_ALU = decoder_2_out0 ? 1'b0 : 1'bz;  // Controlled_Buffer controlled_buffer_7
  assign NEXT_INS_ALU = decoder_2_out2 ? 1'b1 : 1'bz;  // Controlled_Buffer controlled_buffer_8
  assign NEXT_INS_LD = decoder_3_out0 ? 1'b0 : 1'bz;  // Controlled_Buffer controlled_buffer_9
  assign NEXT_INS_LD = decoder_3_out2 ? 1'b1 : 1'bz;  // Controlled_Buffer controlled_buffer_10
  Decoder #(.enable("false")) decoder_7 (.out0(decoder_7_out0), .out1(decoder_7_out1), .sel(counter_3_q));
  assign PC_ENABLE_JUMP = decoder_4_out1 ? 1'b1 : 1'bz;  // Controlled_Buffer controlled_buffer_11
  assign PC_ENABLE_JUMP = decoder_4_out3 ? 1'b0 : 1'bz;  // Controlled_Buffer controlled_buffer_12
  assign controlled_buffer_13_out = decoder_5_out0 ? 1'b1 : 1'bz;  // Controlled_Buffer controlled_buffer_13
  assign NEXT_INS_RESET = decoder_5_out3 ? 1'b0 : 1'bz;  // Controlled_Buffer controlled_buffer_14
  assign NEXT_INS_CMP = decoder_6_out0 ? 1'b1 : 1'bz;  // Controlled_Buffer controlled_buffer_15
  assign NEXT_INS_CMP = decoder_6_out1 ? 1'b0 : 1'bz;  // Controlled_Buffer controlled_buffer_16
  assign MEMORY_ENABLE_ST = decoder_7_out0 ? 1'b0 : 1'bz;  // Controlled_Buffer controlled_buffer_17
  assign MEMORY_ENABLE_ST = decoder_7_out1 ? 1'b1 : 1'bz;  // Controlled_Buffer controlled_buffer_18

  assign ADDRESS = IR_VALUE[9:0];
  assign ALU_R1 = SRC1_VALUE;
  assign CLOCK_CMP = CLOCK;
  assign CLOCK_MEMORY = CLOCK;
  assign CLOCK_PC = CLOCK;
  assign CLOCK_REGFILE = CLOCK;
  assign DST_SRC = IR_VALUE[13:10];
  assign IS_RESET_LED = IS_RESET_CMP;
  assign IS_RESET_REGFILE = IS_RESET_CMP;
  assign NEXT_INS_LED = NEXT_INS;
  assign OP1 = SRC1_VALUE;
  assign OP2 = SRC2_VALUE;
  assign RAM_ADDRESS = IR_VALUE[9:0];
  assign RAM_DATA = SRC1_VALUE;
  assign READ_REG2 = IR_VALUE[3:0];
  assign RESET_PC = RESET_MANUEL;

  // Other names for the same wires on the sheet: cmp = IS_CMP; ld = IS_LD; MEMORY_ENABLE_LD = IS_WRITE_REGFILE_LD;
  //   PC_ENABLE_ALU = NEXT_INS_ALU; PC_ENABLE_CMP = NEXT_INS_CMP; PC_ENABLE_LD = NEXT_INS_LD;
  //   PC_ENABLE_RESET = NEXT_INS_RESET; NEXT_INS_ST = MEMORY_ENABLE_ST; PC_ENABLE_ST = MEMORY_ENABLE_ST;
  //   IMM[5:0] = IR_VALUE[5:0]; SRC2_OP2[3:0] = IR_VALUE[3:0]; SRC1_OP1[3:0] = IR_VALUE[9:6]; IS_RESET = IS_RESET_CMP;
  //   reset = IS_RESET_CMP; st = IS_ST

  // Notes on the sheet:
  //   op1 taşıma şansımız var mı eklemedm
  //   İNPUT
  //   OUTPUT
  //   REGİSTER FİLE okuma yaparken lazım
  //   data memory için adres
  //   regfile yazma için lazım
  //   alu için lazım
  //   cmp için lazım
  //   okunacak adres
  //   SIGNALS
  //   ALU
  //   LD
  //   ST
  //   JUMP
  //   RESET
  //   RESET
  //   ALU FSM
endmodule

module INSTRUCTION_MEMORY (
  input  [9:0] ADDRESS,
  output [17:0] DATA,
  output [9:0] ADDRESS_2
);

  ROM #(.addrWidth(10), .dataWidth(18)) rom_1 (.addr(ADDRESS), .data(DATA), .sel(1'b1));

  assign ADDRESS_2 = ADDRESS;

  // Notes on the sheet:
  //   contents of rom_1 (hex, n*v repeats v):
  //   3c000 18000 18401 18800 18c00 19002 200c4 28006 801 10040 10480 10cc1 243fa 1c40b
endmodule

module MEMORY (
  input  [9:0] ADDRESS,
  input  [17:0] DATA_IN,
  input  IS_ST,
  input  MEMORY_ENABLE,
  input  CLCK,
  input  IS_LD,
  output [9:0] ADDRESS_2,
  output [17:0] DATA_OUT,
  output [17:0] DATA_OUT_2,
  output [17:0] DATA_IN_2,
  output IS_ST_2,
  output MEMORY_ENABLE_2,
  output IS_LD_2
);

  RAM #(.addrWidth(10), .dataWidth(18), .bus("separate")) ram_1 (
    .addr(ADDRESS), .din(DATA_IN), .data(DATA_OUT), .str(IS_ST), .sel(MEMORY_ENABLE), .clk(CLCK), .ld(IS_LD));  // open: clr

  assign ADDRESS_2 = ADDRESS;
  assign DATA_IN_2 = DATA_IN;
  assign DATA_OUT_2 = DATA_OUT;
  assign IS_LD_2 = IS_LD;
  assign IS_ST_2 = IS_ST;
  assign MEMORY_ENABLE_2 = MEMORY_ENABLE;
endmodule
